// Logisim project ProcessadorPipeline-16-Bits.circ as structural Verilog
module ULA (
  input  [31:0] in_1,
  input  [31:0] DATA_0,
  input  [31:0] DATA_1,
  input  [3:0] ULA_OP,
  output [31:0] ULA_OUT,
  output beq,
  output write,
  output load
);

  wire comp_1_jump, comparator_1_eq;
  wire [31:0] adder_1_out, adder_2_out, adder_3_out, multiplier_1_out, subtractor_1_out;

  Adder #(.width(32)) adder_1 (.a(DATA_0), .b(DATA_1), .out(adder_1_out));  // open: cin, cout
  Subtractor #(.width(32)) subtractor_1 (.a(DATA_0), .b(DATA_1), .out(subtractor_1_out));  // open: bin, bout
  Multiplier #(.width(32)) multiplier_1 (.a(DATA_0), .b(DATA_1), .out(multiplier_1_out));  // open: cin, cout
  Adder #(.width(32)) adder_2 (.a(in_1), .b({32{1'b0}}), .out(adder_2_out));  // open: cin, cout
  Comparator #(.width(32), .mode("unsigned")) comparator_1 (
    .a(DATA_1), .b(DATA_0), .eq(comparator_1_eq));  // open: gt, lt
  Adder #(.width(32)) adder_3 (.a(in_1), .b(DATA_0), .out(adder_3_out));  // open: cin, cout
  Multiplexer #(.select(4), .width(32), .enable("false")) multiplexer_1 (
    .in1(subtractor_1_out), .in2(multiplier_1_out), .in4(DATA_0), .in5(adder_1_out), .in6(adder_2_out),
    .in8(adder_3_out), .out(ULA_OUT), .sel(ULA_OP));  // open: in0, in3, in7, in9, in10, in11, in12, in13, in14, in15
  comp comp_1 (.E3(ULA_OP[3]), .E2(ULA_OP[2]), .E1(ULA_OP[1]), .E0(ULA_OP[0]), .jump(comp_1_jump));
  STORE store_1 (.ULA_1(ULA_OP[3]), .ULA_2(ULA_OP[2]), .ULA_3(ULA_OP[1]), .ULA_4(ULA_OP[0]), .STORE(write));
  LOAD load_1 (.ULA_1(ULA_OP[3]), .ULA_2(ULA_OP[2]), .ULA_3(ULA_OP[1]), .ULA_4(ULA_OP[0]), .LOAD(load));
  and and_1 (beq, comparator_1_eq, comp_1_jump);
endmodule

module PROCESSADOR (
  input  in_1
);

  wire and_1_out, and_2_out, and_3_out, beq_1_jump, beq_2_jump, beq_3_jump, button_1_out, clock_1_out,
       ex_mem_1_out_11, ex_mem_1_out_15, ex_mem_1_out_16, hazard_ex_mem_1_ex_mem, hazard_ex_mem_1_out_5,
       hazard_id_ex_1_id_ex, hazard_id_ex_1_out_6, hazard_id_ex_1_out_8, hazard_id_mem_1_id_mem,
       hazard_id_mem_1_out_5, hazard_wb_id_1_ex_mem, hazard_wb_id_1_out_5, hazerd_ex_wd_1_ex_wb,
       hazerd_ex_wd_1_out_5, hazerd_mem_wb_1_mem_wb, id_ex_1_out_9, jump_1_jump, mem_wb_1_out_9,
       mem_wb_1_out_14, operation_unit_1_bubble_control, operation_unit_1_out_19, or_1_out, or_2_out,
       or_3_out, or_4_out, or_5_out, or_6_out, uc_5_1_jump, uc_5_1_write_reg, ula_1_beq, ula_1_load,
       ula_1_write;
  wire [1:0] multiplexer_4_out, multiplexer_10_out, operation_unit_1_out_15, operation_unit_1_out_17,
       operation_unit_1_out_21, operation_unit_1_out_23;
  wire [3:0] ex_mem_1_out_17, id_ex_1_out_14, mem_wb_1_out_13;
  wire [15:0] ex_mem_1_out_12, ex_mem_1_out_12_2, if_id_1_out_4, if_id_1_out_4_2, mem_wb_1_out_10,
       mem_wb_1_out_10_2, multiplexer_3_out, rom_1_data;
  wire [23:0] ex_mem_1_out_13;
  wire [31:0] adder_1_out, banco_de_registradores_1_inteiro, banco_de_registradores_1_r0_d,
       banco_de_registradores_1_r1_d, ex_mem_1_out_14, id_ex_1_out_10, id_ex_1_out_11, id_ex_1_out_12,
       id_ex_1_out_13, mem_wb_1_out_11, mem_wb_1_out_12, multiplexer_1_out, multiplexer_2_out,
       multiplexer_5_out, multiplexer_6_out, multiplexer_7_out, multiplexer_8_out, multiplexer_9_out,
       multiplexer_11_out, multiplexer_12_out, operation_unit_1_ex_mem_out, operation_unit_1_ex_wb_out,
       operation_unit_1_id_mem_out, operation_unit_1_id_wb_out, operation_unit_1_mem_wb_out, ram_1_data,
       register_1_q, ula_1_ula_out;
  wire [31:16] rom_1_data_2;

  or or_1 (or_1_out, ula_1_beq, jump_1_jump);
  Adder #(.width(32)) adder_1 (.a(register_1_q), .b(32'h4), .out(adder_1_out));  // open: cin, cout
  Clock clock_1 (.out(clock_1_out));
  Button button_1 (.out(button_1_out));
  Multiplexer #(.width(32)) multiplexer_1 (
    .in0(adder_1_out), .in1({{16{1'b0}}, multiplexer_3_out}), .out(multiplexer_1_out), .sel(or_1_out));  // open: en
  and and_1 (and_1_out, clock_1_out, ~or_3_out, operation_unit_1_bubble_control);  // AND_Gate
  Multiplexer #(.width(32)) multiplexer_2 (
    .in0(operation_unit_1_id_wb_out), .in1(operation_unit_1_id_mem_out), .out(multiplexer_2_out),
    .sel(operation_unit_1_out_17[0]));  // open: en
  Multiplexer #(.width(16)) multiplexer_3 (
    .in0(rom_1_data), .in1(id_ex_1_out_10[15:0]), .out(multiplexer_3_out), .sel(ula_1_beq));  // open: en
  Register #(.width(32)) register_1 (
    .D(multiplexer_1_out), .Q(register_1_q), .clk(and_1_out), .clr(button_1_out));  // open: en
  Multiplexer #(.width(2)) multiplexer_4 (
    .in0(operation_unit_1_out_23), .in1(operation_unit_1_out_17), .out(multiplexer_4_out),
    .sel(operation_unit_1_out_17[0]));  // open: en
  jump jump_1 (
    .E3(rom_1_data_2[31]), .E2(rom_1_data_2[30]), .E1(rom_1_data_2[29]), .E0(rom_1_data_2[28]),
    .jump(jump_1_jump));
  ROM #(.dataWidth(32)) rom_1 (.addr(register_1_q[9:2]), .data({rom_1_data_2, rom_1_data}));  // open: sel
  and and_2 (and_2_out, operation_unit_1_bubble_control, clock_1_out);  // AND_Gate
  IF_ID if_id_1 (
    .in_1({rom_1_data_2, rom_1_data}), .in_2(and_2_out), .in_3(or_2_out),
    .out_4({if_id_1_out_4_2, if_id_1_out_4}));
  or or_2 (or_2_out, uc_5_1_jump, ula_1_beq, button_1_out);
  beq beq_1 (
    .E3(if_id_1_out_4_2[15]), .E2(if_id_1_out_4_2[14]), .E1(if_id_1_out_4_2[13]), .E0(if_id_1_out_4_2[12]),
    .jump(beq_1_jump));
  UC_5 uc_5_1 (
    .E3(if_id_1_out_4_2[15]), .E2(if_id_1_out_4_2[14]), .E1(if_id_1_out_4_2[13]), .E0(if_id_1_out_4_2[12]),
    .write_reg(uc_5_1_write_reg), .jump(uc_5_1_jump));
  BANCO_DE_REGISTRADORES banco_de_registradores_1 (
    .DATA_WRITE(multiplexer_12_out), .CLK(clock_1_out), .RW(mem_wb_1_out_13),
    .R0_D(banco_de_registradores_1_r0_d), .R0(if_id_1_out_4_2[3:0]), .R1_D(banco_de_registradores_1_r1_d),
    .R1(if_id_1_out_4_2[7:4]), .RW_2(mem_wb_1_out_9), .RESET(button_1_out),
    .inteiro(banco_de_registradores_1_inteiro));
  or or_3 (or_3_out, beq_2_jump, beq_1_jump);
  Multiplexer #(.width(32)) multiplexer_5 (
    .in0(banco_de_registradores_1_r0_d), .in1(multiplexer_2_out), .out(multiplexer_5_out),
    .sel(multiplexer_4_out[0]));  // open: en
  Multiplexer #(.width(32)) multiplexer_6 (
    .in0(banco_de_registradores_1_r1_d), .in1(multiplexer_2_out), .out(multiplexer_6_out),
    .sel(multiplexer_4_out[1]));  // open: en
  LED led_1 (.in(hazerd_ex_wd_1_ex_wb));
  LED led_2 (.in(hazerd_mem_wb_1_mem_wb));
  LED led_3 (.in(hazard_id_mem_1_id_mem));
  LED led_4 (.in(hazard_ex_mem_1_ex_mem));
  HAZARD_ID_EX hazard_id_ex_1 (
    .ID(if_id_1_out_4_2), .EX_W(id_ex_1_out_9), .EX(id_ex_1_out_10[31:16]), .in_4(clock_1_out),
    .in_5(button_1_out), .out_6(hazard_id_ex_1_out_6), .ID_EX(hazard_id_ex_1_id_ex),
    .out_8(hazard_id_ex_1_out_8));
  ID_EX id_ex_1 (
    .RW(uc_5_1_write_reg), .\Instrução ({if_id_1_out_4_2, if_id_1_out_4}), .R0(multiplexer_5_out),
    .INTEIRO(banco_de_registradores_1_inteiro), .R1(multiplexer_6_out), .RW_2(if_id_1_out_4_2[11:8]),
    .in_7(and_3_out), .in_8(or_4_out), .out_9(id_ex_1_out_9), .out_10(id_ex_1_out_10),
    .out_11(id_ex_1_out_11), .out_12(id_ex_1_out_12), .out_13(id_ex_1_out_13), .out_14(id_ex_1_out_14));
  and and_3 (and_3_out, operation_unit_1_bubble_control, clock_1_out);
  or or_4 (or_4_out, button_1_out, beq_3_jump, hazard_id_ex_1_out_6);
  Multiplexer #(.width(32)) multiplexer_7 (
    .in0(operation_unit_1_ex_wb_out), .in1(operation_unit_1_ex_mem_out), .out(multiplexer_7_out),
    .sel(operation_unit_1_out_15[0]));  // open: en
  beq beq_2 (
    .E3(id_ex_1_out_10[31]), .E2(id_ex_1_out_10[30]), .E1(id_ex_1_out_10[29]), .E0(id_ex_1_out_10[28]),
    .jump(beq_2_jump));
  Multiplexer #(.width(32)) multiplexer_8 (
    .in0(id_ex_1_out_11), .in1(multiplexer_7_out), .out(multiplexer_8_out), .sel(multiplexer_10_out[0]));  // open: en
  Multiplexer #(.width(32)) multiplexer_9 (
    .in0(id_ex_1_out_13), .in1(multiplexer_7_out), .out(multiplexer_9_out), .sel(multiplexer_10_out[1]));  // open: en
  Multiplexer #(.width(2)) multiplexer_10 (
    .in0(operation_unit_1_out_21), .in1(operation_unit_1_out_15), .out(multiplexer_10_out),
    .sel(operation_unit_1_out_15[0]));  // open: en
  ULA ula_1 (
    .DATA_0(multiplexer_8_out), .DATA_1(multiplexer_9_out), .ULA_OUT(ula_1_ula_out),
    .ULA_OP(id_ex_1_out_10[31:28]), .load(ula_1_load), .write(ula_1_write), .in_1(id_ex_1_out_12),
    .beq(ula_1_beq));
  OPERATION_UNIT operation_unit_1 (
    .ID_EX(hazard_id_ex_1_id_ex), .EX_MEM(hazard_ex_mem_1_ex_mem), .EX_MEM_FOARD(hazard_ex_mem_1_out_5),
    .ID_MEM(hazard_id_mem_1_id_mem), .ID_MEM_FOARD(hazard_id_mem_1_out_5), .MEM_WB(hazerd_mem_wb_1_mem_wb),
    .EX_WB(hazerd_ex_wd_1_ex_wb), .EX_WB_FOARD(hazerd_ex_wd_1_out_5), .ID_WB(hazard_wb_id_1_ex_mem),
    .ID_WB_FOARD(hazard_wb_id_1_out_5), .MEM_FOARD_DATA(multiplexer_11_out),
    .WB_FOARD_DATA(multiplexer_12_out), .BUBBLE_CONTROL(operation_unit_1_bubble_control),
    .EX_MEM_OUT(operation_unit_1_ex_mem_out), .out_15(operation_unit_1_out_15),
    .ID_MEM_OUT(operation_unit_1_id_mem_out), .out_17(operation_unit_1_out_17),
    .MEM_WB_OUT(operation_unit_1_mem_wb_out), .out_19(operation_unit_1_out_19),
    .EX_WB_OUT(operation_unit_1_ex_wb_out), .out_21(operation_unit_1_out_21),
    .ID_WB_OUT(operation_unit_1_id_wb_out), .out_23(operation_unit_1_out_23));
  or or_5 (or_5_out, hazard_id_ex_1_out_8, clock_1_out);
  HAZARD_EX_MEM hazard_ex_mem_1 (
    .EX(id_ex_1_out_10[31:16]), .MEM_W(ex_mem_1_out_11), .MEM(ex_mem_1_out_12_2),
    .EX_MEM(hazard_ex_mem_1_ex_mem), .out_5(hazard_ex_mem_1_out_5));
  EX_MEM ex_mem_1 (
    .RW(id_ex_1_out_9), .\Instrução (id_ex_1_out_10), .\posiçãoMem (multiplexer_9_out[23:0]),
    .ULA_OUT(ula_1_ula_out), .LOAD(ula_1_load), .STORE(ula_1_write), .RW_2(id_ex_1_out_14), .in_8(or_5_out),
    .in_9(or_6_out), .out_11(ex_mem_1_out_11), .out_12({ex_mem_1_out_12_2, ex_mem_1_out_12}),
    .out_13(ex_mem_1_out_13), .out_14(ex_mem_1_out_14), .out_15(ex_mem_1_out_15), .out_16(ex_mem_1_out_16),
    .out_17(ex_mem_1_out_17));  // open: out_10
  or or_6 (or_6_out, or_4_out, button_1_out);
  Multiplexer #(.width(32)) multiplexer_11 (
    .in0(ex_mem_1_out_14), .in1(operation_unit_1_mem_wb_out), .out(multiplexer_11_out),
    .sel(operation_unit_1_out_19));  // open: en
  beq beq_3 (
    .E3(ex_mem_1_out_12_2[15]), .E2(ex_mem_1_out_12_2[14]), .E1(ex_mem_1_out_12_2[13]),
    .E0(ex_mem_1_out_12_2[12]), .jump(beq_3_jump));
  HAZARD_ID_MEM hazard_id_mem_1 (
    .ID(if_id_1_out_4_2), .MEM_W(ex_mem_1_out_11), .MEM(ex_mem_1_out_12_2), .ID_MEM(hazard_id_mem_1_id_mem),
    .out_5(hazard_id_mem_1_out_5));
  RAM #(.addrWidth(24), .dataWidth(32), .bus("separate")) ram_1 (
    .addr(ex_mem_1_out_13), .din(multiplexer_11_out), .data(ram_1_data), .str(ex_mem_1_out_16),
    .clk(clock_1_out), .ld(ex_mem_1_out_15));  // open: sel, clr
  HAZERD_MEM_WB hazerd_mem_wb_1 (
    .MEM(ex_mem_1_out_12_2), .MEM_STR(ex_mem_1_out_16), .WB_W(mem_wb_1_out_9), .WB(mem_wb_1_out_10_2),
    .MEM_WB(hazerd_mem_wb_1_mem_wb));
  MEM_WB mem_wb_1 (
    .RW(ex_mem_1_out_11), .in_2({ex_mem_1_out_12_2, ex_mem_1_out_12}), .saidaMem(ram_1_data),
    .saidaUla(multiplexer_11_out), .Rw_2(ex_mem_1_out_17), .LOAD(ex_mem_1_out_15), .in_7(clock_1_out),
    .in_8(button_1_out), .out_9(mem_wb_1_out_9), .out_10({mem_wb_1_out_10_2, mem_wb_1_out_10}),
    .out_11(mem_wb_1_out_11), .out_12(mem_wb_1_out_12), .out_13(mem_wb_1_out_13), .out_14(mem_wb_1_out_14));
  HAZERD_EX_WD hazerd_ex_wd_1 (
    .EX(id_ex_1_out_10[31:16]), .WB_W(mem_wb_1_out_9), .WB(mem_wb_1_out_10_2), .EX_WB(hazerd_ex_wd_1_ex_wb),
    .out_5(hazerd_ex_wd_1_out_5));
  Multiplexer #(.width(32)) multiplexer_12 (
    .in0(mem_wb_1_out_12), .in1(mem_wb_1_out_11), .out(multiplexer_12_out), .sel(mem_wb_1_out_14));  // open: en
  HAZARD_WB_ID hazard_wb_id_1 (
    .ID(if_id_1_out_4_2), .WB_W(mem_wb_1_out_9), .WB(mem_wb_1_out_10_2), .EX_MEM(hazard_wb_id_1_ex_mem),
    .out_5(hazard_wb_id_1_out_5));

  // Notes on the sheet:
  //   contents of rom_1 (hex, n*v repeats v):
  //   63220000 61000000 62110000 60330000 31110000 32220000 33330000 67000000 68000000 69000000 90000048
  //   87170000 70700094 68000000 90000044 88180000 7080002c 69000000 7009003c 24700000 54490000 54410000
  //   34440000 25900000 55580000 55520000 35550000 26700000 56680000 56630000 3a660000 25450000 5aa50000
  //   406a0000 66000000 89190000 90000048 90000094
endmodule

module UC (
  input  E3,
  input  E2,
  input  E1,
  input  E0,
  output ula_op,
  output write_reg,
  output jump
);

  wire not_1_out, not_2_out, not_3_out;

  not not_1 (not_1_out, E3);
  and and_1 (write_reg, not_1_out, not_2_out, not_3_out);
  not not_2 (not_2_out, E2);
  not not_3 (not_3_out, E1);
  jump jump_1 (.E3(E3), .E2(E2), .E1(E1), .E0(E0), .jump(jump));

  assign ula_op = E0;
endmodule

// REGISTRADORES
module BANCO_DE_REGISTRADORES (
  input  [31:0] DATA_WRITE,
  input  [3:0] R0,
  input  [3:0] R1,
  input  CLK,
  input  [3:0] RW,
  input  RW_2,
  input  RESET,
  output [31:0] inteiro,
  output [31:0] R0_D,
  output [31:0] R1_D
);

  wire demultiplexer_1_out0, demultiplexer_1_out1, demultiplexer_1_out2, demultiplexer_1_out3,
       demultiplexer_1_out4, demultiplexer_1_out5, demultiplexer_1_out6, demultiplexer_1_out7,
       demultiplexer_1_out8, demultiplexer_1_out9, demultiplexer_1_out10, demultiplexer_1_out11,
       demultiplexer_1_out12, demultiplexer_1_out13, demultiplexer_1_out14, demultiplexer_1_out15;
  wire [31:0] register_1_q, register_2_q, register_3_q, register_4_q, register_5_q, register_6_q,
       register_7_q, register_8_q, register_9_q, register_10_q, register_11_q, register_12_q, register_13_q,
       register_14_q, register_15_q, register_16_q;

  Demultiplexer #(.select(4), .enable("false")) demultiplexer_1 (
    .out0(demultiplexer_1_out0), .out1(demultiplexer_1_out1), .out2(demultiplexer_1_out2),
    .out3(demultiplexer_1_out3), .out4(demultiplexer_1_out4), .out5(demultiplexer_1_out5),
    .out6(demultiplexer_1_out6), .out7(demultiplexer_1_out7), .out8(demultiplexer_1_out8),
    .out9(demultiplexer_1_out9), .out10(demultiplexer_1_out10), .out11(demultiplexer_1_out11),
    .out12(demultiplexer_1_out12), .out13(demultiplexer_1_out13), .out14(demultiplexer_1_out14),
    .out15(demultiplexer_1_out15), .in(RW_2), .sel(RW));
  Register #(.width(32)) register_1 (
    .D(DATA_WRITE), .en(demultiplexer_1_out0), .Q(register_1_q), .clk(CLK), .clr(RESET));
  Register #(.width(32)) register_2 (
    .D(DATA_WRITE), .en(demultiplexer_1_out1), .Q(register_2_q), .clk(CLK), .clr(RESET));
  Register #(.width(32)) register_3 (
    .D(DATA_WRITE), .en(demultiplexer_1_out2), .Q(register_3_q), .clk(CLK), .clr(RESET));
  Register #(.width(32)) register_4 (
    .D(DATA_WRITE), .en(demultiplexer_1_out3), .Q(register_4_q), .clk(CLK), .clr(RESET));
  Register #(.width(32)) register_5 (
    .D(DATA_WRITE), .en(demultiplexer_1_out4), .Q(register_5_q), .clk(CLK), .clr(RESET));
  Register #(.width(32)) register_6 (
    .D(DATA_WRITE), .en(demultiplexer_1_out5), .Q(register_6_q), .clk(CLK), .clr(RESET));
  Register #(.width(32)) register_7 (
    .D(DATA_WRITE), .en(demultiplexer_1_out6), .Q(register_7_q), .clk(CLK), .clr(RESET));
  Register #(.width(32)) register_8 (
    .D(DATA_WRITE), .en(demultiplexer_1_out7), .Q(register_8_q), .clk(CLK), .clr(RESET));
  Register #(.width(32)) register_9 (
    .D(DATA_WRITE), .en(demultiplexer_1_out8), .Q(register_9_q), .clk(CLK), .clr(RESET));
  Register #(.width(32)) register_10 (
    .D(DATA_WRITE), .en(demultiplexer_1_out9), .Q(register_10_q), .clk(CLK), .clr(RESET));
  Register #(.width(32)) register_11 (
    .D(DATA_WRITE), .en(demultiplexer_1_out10), .Q(register_11_q), .clk(CLK), .clr(RESET));
  Register #(.width(32)) register_12 (
    .D(DATA_WRITE), .en(demultiplexer_1_out11), .Q(register_12_q), .clk(CLK), .clr(RESET));
  Register #(.width(32)) register_13 (
    .D(DATA_WRITE), .en(demultiplexer_1_out12), .Q(register_13_q), .clk(CLK), .clr(RESET));
  Register #(.width(32)) register_14 (
    .D(DATA_WRITE), .en(demultiplexer_1_out13), .Q(register_14_q), .clk(CLK), .clr(RESET));
  Register #(.width(32)) register_15 (
    .D(DATA_WRITE), .en(demultiplexer_1_out14), .Q(register_15_q), .clk(CLK), .clr(RESET));
  Register #(.width(32)) register_16 (
    .D(DATA_WRITE), .en(demultiplexer_1_out15), .Q(register_16_q), .clk(CLK), .clr(RESET));
  Multiplexer #(.select(4), .width(32), .disabled(0), .enable("false")) multiplexer_1 (
    .in0(register_1_q), .in1(register_2_q), .in2(register_3_q), .in3(register_4_q), .in4(register_5_q),
    .in5(register_6_q), .in6(register_7_q), .in7(register_8_q), .in8(register_9_q), .in9(register_10_q),
    .in10(register_11_q), .in11(register_12_q), .in12(register_13_q), .in13(register_14_q),
    .in14(register_15_q), .in15(register_16_q), .out(R0_D), .sel(R0));
  Multiplexer #(.select(4), .width(32), .enable("false")) multiplexer_2 (
    .in0(register_1_q), .in1(register_2_q), .in2(register_3_q), .in3(register_4_q), .in4(register_5_q),
    .in5(register_6_q), .in6(register_7_q), .in7(register_8_q), .in8(register_9_q), .in9(register_10_q),
    .in10(register_11_q), .in11(register_12_q), .in12(register_13_q), .in13(register_14_q),
    .in14(register_15_q), .in15(register_16_q), .out(R1_D), .sel(R1));

  assign inteiro = {{28{1'b0}}, R1};
endmodule

// UC
module UC_5 (
  input  E3,
  input  E2,
  input  E1,
  input  E0,
  output write_reg,
  output jump
);

  wire and_1_out, and_2_out, and_3_out, and_4_out, not_1_out, not_2_out, not_3_out, not_4_out, not_5_out,
       not_6_out, not_7_out, not_8_out;

  not not_1 (not_1_out, E3);
  not not_2 (not_2_out, E1);
  and and_1 (and_1_out, not_1_out, not_2_out, E0);
  not not_3 (not_3_out, E3);
  and and_2 (and_2_out, not_3_out, not_4_out, E1);
  not not_4 (not_4_out, E2);
  not not_5 (not_5_out, E3);
  and and_3 (and_3_out, not_5_out, E1, not_6_out);
  not not_6 (not_6_out, E0);
  not not_7 (not_7_out, E2);
  and and_4 (and_4_out, E3, not_7_out, not_8_out);
  not not_8 (not_8_out, E1);
  jump jump_1 (.E3(E3), .E2(E2), .E1(E1), .E0(E0), .jump(jump));
  or or_1 (write_reg, and_1_out, and_2_out, and_3_out, and_4_out);
endmodule

module LOAD (
  input  ULA_1,
  input  ULA_2,
  input  ULA_3,
  input  ULA_4,
  output LOAD
);

  wire not_1_out, not_2_out;

  not not_1 (not_1_out, ULA_1);
  not not_2 (not_2_out, ULA_2);
  and and_1 (LOAD, not_1_out, not_2_out, ULA_3, ULA_4);
endmodule

module STORE (
  input  ULA_1,
  input  ULA_2,
  input  ULA_3,
  input  ULA_4,
  output STORE
);

  wire not_1_out, not_2_out, not_3_out;

  not not_1 (not_1_out, ULA_1);
  not not_2 (not_2_out, ULA_3);
  not not_3 (not_3_out, ULA_4);
  and and_1 (STORE, not_1_out, ULA_2, not_2_out, not_3_out);
endmodule

// UC
module UC_4 (
  input  E3,
  input  E2,
  input  E1,
  input  E0,
  output write_reg,
  output jump
);

  wire and_1_out, and_2_out, and_3_out, and_4_out;

  and and_1 (and_1_out, ~E3, ~E2);  // AND_Gate
  and and_2 (and_2_out, ~E2, ~E1, ~E0);  // AND_Gate
  and and_3 (and_3_out, ~E2, ~E1, E0);  // AND_Gate
  and and_4 (and_4_out, ~E3, E1, ~E0);  // AND_Gate
  jump jump_1 (.E3(E3), .E2(E2), .E1(E1), .E0(E0), .jump(jump));
  or or_1 (write_reg, and_1_out, and_2_out, and_3_out, and_4_out);
endmodule

module jump (
  input  E3,
  input  E2,
  input  E1,
  input  E0,
  output jump
);

  wire and_1_out, and_2_out, not_1_out;

  not not_1 (not_1_out, E1);
  and and_1 (and_1_out, E3, not_1_out, E0);
  and and_2 (and_2_out, E3, E2, E0);
  or or_1 (jump, and_1_out, and_2_out);
endmodule

module comp (
  input  E3,
  input  E2,
  input  E1,
  input  E0,
  output jump
);

  wire and_1_out, and_2_out;

  and and_1 (and_1_out, E2, E1, E0);
  and and_2 (and_2_out, E3, E2, E0);
  or or_1 (jump, and_1_out, and_2_out);
endmodule

module loadp (
  input  E3,
  input  E2,
  input  E1,
  input  E0,
  output load
);

  wire not_1_out, not_2_out;

  not not_1 (not_1_out, E3);
  not not_2 (not_2_out, E2);
  and and_1 (load, not_1_out, not_2_out, E1, E0);
endmodule

module storep (
  input  E3,
  input  E2,
  input  E1,
  input  E0,
  output store
);

  wire not_1_out, not_2_out, not_3_out;

  not not_1 (not_1_out, E3);
  not not_2 (not_2_out, E1);
  not not_3 (not_3_out, E0);
  and and_1 (store, not_1_out, E2, not_2_out, not_3_out);
endmodule

module IF_ID (
  input  [31:0] in_1,
  input  in_2,
  input  in_3,
  output [31:0] out_4
);

  Register #(.width(32)) register_1 (.D(in_1), .Q(out_4), .clk(in_2), .clr(in_3));  // open: en
endmodule

module ID_EX (
  input  RW,
  input  [31:0] \Instrução ,
  input  [31:0] R0,
  input  [31:0] INTEIRO,
  input  [31:0] R1,
  input  [3:0] RW_2,
  input  in_7,
  input  in_8,
  output out_9,
  output [31:0] out_10,
  output [31:0] out_11,
  output [31:0] out_12,
  output [31:0] out_13,
  output [3:0] out_14
);

  Register #(.width(1)) register_1 (.D(RW), .Q(out_9), .clk(in_7), .clr(in_8));  // open: en
  Register #(.width(32)) register_2 (.D(\Instrução ), .Q(out_10), .clk(in_7), .clr(in_8));  // open: en
  Register #(.width(32)) register_3 (.D(R0), .Q(out_11), .clk(in_7), .clr(in_8));  // open: en
  Register #(.width(32)) register_4 (.D(INTEIRO), .Q(out_12), .clk(in_7), .clr(in_8));  // open: en
  Register #(.width(32)) register_5 (.D(R1), .Q(out_13), .clk(in_7), .clr(in_8));  // open: en
  Register #(.width(4)) register_6 (.D(RW_2), .Q(out_14), .clk(in_7), .clr(in_8));  // open: en
endmodule

module EX_MEM (
  input  RW,
  input  [31:0] \Instrução ,
  input  [23:0] \posiçãoMem ,
  input  [31:0] ULA_OUT,
  input  LOAD,
  input  STORE,
  input  [3:0] RW_2,
  input  in_8,
  input  in_9,
  output out_10,
  output out_11,
  output [31:0] out_12,
  output [23:0] out_13,
  output [31:0] out_14,
  output out_15,
  output out_16,
  output [3:0] out_17
);

  wire comparator_1_eq, comparator_2_eq;

  Comparator #(.width(32), .mode("unsigned")) comparator_1 (
    .a({32{1'b0}}), .b(\Instrução ), .eq(comparator_1_eq));  // open: gt, lt
  and and_1 (out_10, comparator_2_eq, ~comparator_1_eq);  // AND_Gate
  Comparator #(.width(32), .mode("unsigned")) comparator_2 (
    .a(\Instrução ), .b(out_12), .eq(comparator_2_eq));  // open: gt, lt
  Register #(.width(1)) register_1 (.D(RW), .Q(out_11), .clk(in_8), .clr(in_9));  // open: en
  Register #(.width(32)) register_2 (.D(\Instrução ), .Q(out_12), .clk(in_8), .clr(in_9));  // open: en
  Register #(.width(24)) register_3 (.D(\posiçãoMem ), .Q(out_13), .clk(in_8), .clr(in_9));  // open: en
  Register #(.width(32)) register_4 (.D(ULA_OUT), .Q(out_14), .clk(in_8), .clr(in_9));  // open: en
  Register #(.width(1)) register_5 (.D(LOAD), .Q(out_15), .clk(in_8), .clr(in_9));  // open: en
  Register #(.width(1)) register_6 (.D(STORE), .Q(out_16), .clk(in_8), .clr(in_9));  // open: en
  Register #(.width(4)) register_7 (.D(RW_2), .Q(out_17), .clk(in_8), .clr(in_9));  // open: en
endmodule

module MEM_WB (
  input  RW,
  input  [31:0] in_2,
  input  [31:0] saidaMem,
  input  [31:0] saidaUla,
  input  [3:0] Rw_2,
  input  LOAD,
  input  in_7,
  input  in_8,
  output out_9,
  output [31:0] out_10,
  output [31:0] out_11,
  output [31:0] out_12,
  output [3:0] out_13,
  output out_14
);

  Register #(.width(1)) register_1 (.D(RW), .Q(out_9), .clk(in_7), .clr(in_8));  // open: en
  Register #(.width(32)) register_2 (.D(in_2), .Q(out_10), .clk(in_7), .clr(in_8));  // open: en
  Register #(.width(32)) register_3 (.D(saidaMem), .Q(out_11), .clk(in_7), .clr(in_8));  // open: en
  Register #(.width(32)) register_4 (.D(saidaUla), .Q(out_12), .clk(in_7), .clr(in_8));  // open: en
  Register #(.width(4)) register_5 (.D(Rw_2), .Q(out_13), .clk(in_7), .clr(in_8));  // open: en
  Register #(.width(1)) register_6 (.D(LOAD), .Q(out_14), .clk(in_7), .clr(in_8));  // open: en
endmodule

module HAZARD_ID_EX (
  input  [15:0] ID,
  input  EX_W,
  input  [15:0] EX,
  input  in_4,
  input  in_5,
  output out_6,
  output ID_EX,
  output out_8
);

  wire and_1_out, and_2_out, comparator_1_eq, comparator_2_eq, comparator_3_eq, comparator_4_eq,
       comparator_5_eq, or_1_out, or_2_out, or_3_out, register_1_q, seletor_1_out_6;

  Comparator #(.width(4), .mode("unsigned")) comparator_1 (
    .a(ID[3:0]), .b(EX[11:8]), .eq(comparator_1_eq));  // open: gt, lt
  Comparator #(.width(4), .mode("unsigned")) comparator_2 (
    .a(ID[7:4]), .b(EX[11:8]), .eq(comparator_2_eq));  // open: gt, lt
  Comparator #(.width(4), .mode("unsigned")) comparator_3 (
    .a(ID[15:12]), .b(4'b0000), .eq(comparator_3_eq));  // open: gt, lt
  Comparator #(.width(4), .mode("unsigned")) comparator_4 (
    .a(ID[15:12]), .b(4'b0110), .eq(comparator_4_eq));  // open: gt, lt
  Comparator #(.width(4), .mode("unsigned")) comparator_5 (
    .a(4'b0000), .b(ID[15:12]), .eq(comparator_5_eq));  // open: gt, lt
  or or_1 (or_1_out, comparator_1_eq, comparator_2_eq);
  or or_2 (or_2_out, comparator_3_eq, comparator_5_eq, comparator_4_eq);
  and and_1 (and_1_out, EX_W, ~seletor_1_out_6, or_1_out, ~or_2_out);  // AND_Gate
  Register #(.width(1)) register_1 (.D(and_1_out), .Q(register_1_q), .clk(in_4), .clr(in_5));  // open: en
  and and_2 (and_2_out, in_4, register_1_q);
  seletor seletor_1 (
    .in_1(and_2_out), .clr(or_3_out), .out_4(out_8), .out_5(out_6), .out_6(seletor_1_out_6));  // open: out_3
  or or_3 (or_3_out, seletor_1_out_6, in_5);
  or or_4 (ID_EX, register_1_q, and_1_out);
endmodule

module HAZARD_EX_MEM (
  input  [15:0] EX,
  input  MEM_W,
  input  [15:0] MEM,
  output EX_MEM,
  output out_5
);

  wire comparator_1_eq, comparator_2_eq, comparator_3_eq, comparator_4_eq, comparator_5_eq, or_1_out,
       or_2_out;

  Comparator #(.width(4), .mode("unsigned")) comparator_1 (
    .a(EX[3:0]), .b(MEM[11:8]), .eq(comparator_1_eq));  // open: gt, lt
  Comparator #(.width(4), .mode("unsigned")) comparator_2 (
    .a(EX[7:4]), .b(MEM[11:8]), .eq(comparator_2_eq));  // open: gt, lt
  Comparator #(.width(4), .mode("unsigned")) comparator_3 (
    .a(EX[15:12]), .b(4'b0000), .eq(comparator_3_eq));  // open: gt, lt
  Comparator #(.width(4), .mode("unsigned")) comparator_4 (
    .a(MEM[15:12]), .b(4'b0110), .eq(comparator_4_eq));  // open: gt, lt
  Comparator #(.width(4), .mode("unsigned")) comparator_5 (
    .a(MEM[15:12]), .b(EX[15:12]), .eq(comparator_5_eq));  // open: gt, lt
  or or_1 (or_1_out, comparator_1_eq, comparator_2_eq);
  or or_2 (or_2_out, comparator_3_eq, comparator_5_eq, comparator_4_eq);
  and and_1 (EX_MEM, MEM_W, ~or_2_out, or_1_out);  // AND_Gate
  Multiplexer multiplexer_1 (.in0(1'b0), .in1(1'b1), .out(out_5), .sel(comparator_2_eq));  // open: en
endmodule

module HAZARD_ID_MEM (
  input  [15:0] ID,
  input  MEM_W,
  input  [15:0] MEM,
  output ID_MEM,
  output out_5
);

  wire comparator_1_eq, comparator_2_eq, comparator_3_eq, comparator_4_eq, comparator_5_eq, or_1_out,
       or_2_out;

  Comparator #(.width(4), .mode("unsigned")) comparator_1 (
    .a(ID[15:12]), .b(4'b0000), .eq(comparator_1_eq));  // open: gt, lt
  Comparator #(.width(4), .mode("unsigned")) comparator_2 (
    .a(MEM[15:12]), .b(4'b0110), .eq(comparator_2_eq));  // open: gt, lt
  Comparator #(.width(4), .mode("unsigned")) comparator_3 (
    .a(4'b0000), .b(MEM[15:12]), .eq(comparator_3_eq));  // open: gt, lt
  Comparator #(.width(4), .mode("unsigned")) comparator_4 (
    .a(ID[3:0]), .b(MEM[11:8]), .eq(comparator_4_eq));  // open: gt, lt
  Comparator #(.width(4), .mode("unsigned")) comparator_5 (
    .a(ID[7:4]), .b(MEM[11:8]), .eq(comparator_5_eq));  // open: gt, lt
  or or_1 (or_1_out, comparator_1_eq, comparator_3_eq, comparator_2_eq);
  or or_2 (or_2_out, comparator_4_eq, comparator_5_eq);
  and and_1 (ID_MEM, MEM_W, ~or_1_out, or_2_out);  // AND_Gate
  Multiplexer multiplexer_1 (.in0(1'b0), .in1(1'b1), .out(out_5), .sel(comparator_5_eq));  // open: en

  // Notes on the sheet:
  //   ID_MEM
endmodule

module HAZERD_MEM_WB (
  input  [15:0] MEM,
  input  MEM_STR,
  input  WB_W,
  input  [15:0] WB,
  output MEM_WB
);

  wire and_1_out, comparator_1_eq, comparator_2_eq, comparator_3_eq, comparator_4_eq, comparator_5_eq,
       or_1_out, or_2_out;

  and and_1 (and_1_out, MEM_STR, WB_W);
  Comparator #(.width(4), .mode("unsigned")) comparator_1 (
    .a(MEM[3:0]), .b(WB[11:8]), .eq(comparator_1_eq));  // open: gt, lt
  Comparator #(.width(4), .mode("unsigned")) comparator_2 (
    .a(MEM[7:4]), .b(WB[11:8]), .eq(comparator_2_eq));  // open: gt, lt
  Comparator #(.width(4), .mode("unsigned")) comparator_3 (
    .a(MEM[15:12]), .b(4'b0110), .eq(comparator_3_eq));  // open: gt, lt
  Comparator #(.width(4), .mode("unsigned")) comparator_4 (
    .a(MEM[15:12]), .b(4'b0000), .eq(comparator_4_eq));  // open: gt, lt
  Comparator #(.width(4), .mode("unsigned")) comparator_5 (
    .a(MEM[15:12]), .b(4'b0000), .eq(comparator_5_eq));  // open: gt, lt
  or or_1 (or_1_out, comparator_1_eq, comparator_2_eq);
  or or_2 (or_2_out, comparator_3_eq, comparator_5_eq, comparator_4_eq);
  and and_2 (MEM_WB, and_1_out, ~or_2_out, or_1_out);  // AND_Gate

  // Notes on the sheet:
  //   EX-MEM
endmodule

module HAZERD_EX_WD (
  input  [15:0] EX,
  input  WB_W,
  input  [15:0] WB,
  output EX_WB,
  output out_5
);

  wire comparator_1_eq, comparator_2_eq, comparator_3_eq, comparator_4_eq, comparator_5_eq, or_1_out,
       or_2_out;

  Comparator #(.width(4), .mode("unsigned")) comparator_1 (
    .a(EX[15:12]), .b(4'b0110), .eq(comparator_1_eq));  // open: gt, lt
  Comparator #(.width(4), .mode("unsigned")) comparator_2 (
    .a(EX[15:12]), .b(4'b0000), .eq(comparator_2_eq));  // open: gt, lt
  Comparator #(.width(4), .mode("unsigned")) comparator_3 (
    .a(4'b0000), .b(EX[15:12]), .eq(comparator_3_eq));  // open: gt, lt
  Comparator #(.width(4), .mode("unsigned")) comparator_4 (
    .a(EX[3:0]), .b(WB[11:8]), .eq(comparator_4_eq));  // open: gt, lt
  Comparator #(.width(4), .mode("unsigned")) comparator_5 (
    .a(EX[7:4]), .b(WB[11:8]), .eq(comparator_5_eq));  // open: gt, lt
  or or_1 (or_1_out, comparator_1_eq, comparator_3_eq, comparator_2_eq);
  or or_2 (or_2_out, comparator_4_eq, comparator_5_eq);
  and and_1 (EX_WB, WB_W, ~or_1_out, or_2_out);  // AND_Gate
  Multiplexer multiplexer_1 (.in0(1'b0), .in1(1'b1), .out(out_5), .sel(comparator_5_eq));  // open: en

  // Notes on the sheet:
  //   EX_WD
endmodule

module HAZARD_WB_ID (
  input  [15:0] ID,
  input  WB_W,
  input  [15:0] WB,
  output EX_MEM,
  output out_5
);

  wire comparator_1_eq, comparator_2_eq, comparator_3_eq, comparator_4_eq, comparator_5_eq, or_1_out,
       or_2_out;

  Comparator #(.width(4), .mode("unsigned")) comparator_1 (
    .a(ID[3:0]), .b(WB[11:8]), .eq(comparator_1_eq));  // open: gt, lt
  Comparator #(.width(4), .mode("unsigned")) comparator_2 (
    .a(ID[7:4]), .b(WB[11:8]), .eq(comparator_2_eq));  // open: gt, lt
  Comparator #(.width(4), .mode("unsigned")) comparator_3 (
    .a(ID[15:12]), .b(4'b0000), .eq(comparator_3_eq));  // open: gt, lt
  Comparator #(.width(4), .mode("unsigned")) comparator_4 (
    .a(ID[15:12]), .b(4'b0110), .eq(comparator_4_eq));  // open: gt, lt
  Comparator #(.width(4), .mode("unsigned")) comparator_5 (
    .a(4'b0000), .b(WB[11:8]), .eq(comparator_5_eq));  // open: gt, lt
  or or_1 (or_1_out, comparator_1_eq, comparator_2_eq);
  or or_2 (or_2_out, comparator_3_eq, comparator_5_eq, comparator_4_eq);
  and and_1 (EX_MEM, WB_W, ~or_2_out, or_1_out);  // AND_Gate
  Multiplexer multiplexer_1 (.in0(1'b0), .in1(1'b1), .out(out_5), .sel(comparator_2_eq));  // open: en
endmodule

module OPERATION_UNIT (
  input  ID_EX,
  input  EX_MEM,
  input  EX_MEM_FOARD,
  input  ID_MEM,
  input  ID_MEM_FOARD,
  input  MEM_WB,
  input  EX_WB,
  input  EX_WB_FOARD,
  input  ID_WB,
  input  ID_WB_FOARD,
  input  [31:0] MEM_FOARD_DATA,
  input  [31:0] WB_FOARD_DATA,
  output BUBBLE_CONTROL,
  output [31:0] EX_MEM_OUT,
  output [1:0] out_15,
  output [31:0] ID_MEM_OUT,
  output [1:0] out_17,
  output [31:0] MEM_WB_OUT,
  output out_19,
  output [31:0] EX_WB_OUT,
  output [1:0] out_21,
  output [31:0] ID_WB_OUT,
  output [1:0] out_23
);

  not not_1 (BUBBLE_CONTROL, ID_EX);
  and and_1 (out_15[0], EX_MEM, ~EX_MEM_FOARD);  // AND_Gate
  and and_2 (out_15[1], EX_MEM, EX_MEM_FOARD);
  and and_3 (out_17[0], ID_MEM, ~ID_MEM_FOARD);  // AND_Gate
  and and_4 (out_17[1], ID_MEM, ID_MEM_FOARD);
  and and_5 (out_21[0], EX_WB, ~EX_WB_FOARD);  // AND_Gate
  and and_6 (out_21[1], EX_WB, EX_WB_FOARD);
  and and_7 (out_23[0], ID_WB, ~ID_WB_FOARD);  // AND_Gate
  and and_8 (out_23[1], ID_WB, ID_WB_FOARD);

  assign EX_MEM_OUT = MEM_FOARD_DATA;
  assign EX_WB_OUT = WB_FOARD_DATA;
  assign ID_MEM_OUT = MEM_FOARD_DATA;
  assign ID_WB_OUT = WB_FOARD_DATA;
  assign MEM_WB_OUT = WB_FOARD_DATA;
  assign out_19 = MEM_WB;
endmodule

module aux_1 (
  input  in_1,
  input  in_2,
  output out_3,
  output out_4
);

  wire and_1_out, and_2_out;

  and and_1 (and_1_out, ~in_1, in_2);  // AND_Gate
  and and_2 (and_2_out, in_1, ~in_2);  // AND_Gate
  not not_1 (out_4, in_2);
  or or_1 (out_3, and_1_out, and_2_out);
endmodule

module seletor (
  input  in_1,
  input  clr,
  output out_3,
  output out_4,
  output out_5,
  output out_6
);

  wire aux_1_1_out_3, aux_1_1_out_4, d_ff_1_q, d_ff_2_q;

  D_Flip_Flop d_ff_1 (.clk(in_1), .D(aux_1_1_out_4), .Q(d_ff_1_q), .reset(clr));  // open: Qn, preset, en
  D_Flip_Flop d_ff_2 (.clk(in_1), .D(aux_1_1_out_3), .Q(d_ff_2_q), .reset(clr));  // open: Qn, preset, en
  aux_1 aux_1_1 (.in_1(d_ff_2_q), .in_2(d_ff_1_q), .out_3(aux_1_1_out_3), .out_4(aux_1_1_out_4));
  and and_1 (out_3, ~d_ff_2_q, ~d_ff_1_q);  // AND_Gate
  and and_2 (out_4, ~d_ff_2_q, d_ff_1_q);  // AND_Gate
  and and_3 (out_5, d_ff_2_q, ~d_ff_1_q);  // AND_Gate
  and and_4 (out_6, d_ff_2_q, d_ff_1_q);
endmodule

module beq (
  input  E3,
  input  E2,
  input  E1,
  input  E0,
  output jump
);

  wire not_1_out;

  not not_1 (not_1_out, E3);
  and and_1 (jump, not_1_out, E2, E1, E0);
endmodule
