// Logisim project mips-like.circ as structural Verilog: 10 circuits, main circuit ULA
module PROCESSADOR (
);

  wire button_1_out, clock_1_out, or_1_out, uc_4_1_jump, uc_4_1_write_reg, ula_1_bgt, ula_1_load, ula_1_write;
  wire [3:0] uc_4_1_out_6;
  wire [15:0] rom_1_data;
  wire [31:0] adder_1_out, banco_de_registradores_1_inteiro, banco_de_registradores_1_r0_d,
       banco_de_registradores_1_r1_d, multiplexer_1_out, multiplexer_2_out, multiplexer_3_out, ram_1_data,
       register_1_q, ula_1_ula_out;
  wire [31:16] rom_1_data_2;

  or or_1 (or_1_out, ula_1_bgt, uc_4_1_jump);
  Adder #(.width(32)) adder_1 (.a(register_1_q), .b(32'h4), .out(adder_1_out));  // open: cin, cout
  Clock clock_1 (.out(clock_1_out));
  Button button_1 (.out(button_1_out));
  Multiplexer #(.width(32)) multiplexer_1 (
    .in0(adder_1_out), .in1({{16{1'b0}}, rom_1_data}), .out(multiplexer_1_out), .sel(or_1_out));  // open: en
  Register #(.width(32)) register_1 (
    .D(multiplexer_1_out), .Q(register_1_q), .clk(clock_1_out), .clr(button_1_out));  // open: en
  ROM #(.dataWidth(32)) rom_1 (.addr(register_1_q[9:2]), .data({rom_1_data_2, rom_1_data}));  // open: sel
  UC_4 uc_4_1 (
    .E3(rom_1_data_2[31]), .E2(rom_1_data_2[30]), .E1(rom_1_data_2[29]), .E0(rom_1_data_2[28]),
    .write_reg(uc_4_1_write_reg), .out_6(uc_4_1_out_6), .jump(uc_4_1_jump));
  BANCO_DE_REGISTRADORES banco_de_registradores_1 (
    .DATA_WRITE(multiplexer_3_out), .CLK(clock_1_out), .RW(rom_1_data_2[27:24]),
    .R0_D(banco_de_registradores_1_r0_d), .R0(rom_1_data_2[19:16]), .R1_D(banco_de_registradores_1_r1_d),
    .R1(rom_1_data_2[23:20]), .RW_2(uc_4_1_write_reg), .RESET(button_1_out),
    .inteiro(banco_de_registradores_1_inteiro));
  ULA ula_1 (
    .DATA_0(banco_de_registradores_1_r0_d), .DATA_1(banco_de_registradores_1_r1_d), .ULA_OUT(ula_1_ula_out),
    .ULA_OP(uc_4_1_out_6), .load(ula_1_load), .write(ula_1_write), .in_1(banco_de_registradores_1_inteiro),
    .bgt(ula_1_bgt));
  Multiplexer #(.width(32)) multiplexer_2 (
    .in0(ula_1_ula_out), .in1(banco_de_registradores_1_r1_d), .out(multiplexer_2_out), .sel(ula_1_write));  // open: en
  RAM #(.addrWidth(24), .dataWidth(32), .bus("separate")) ram_1 (
    .addr(banco_de_registradores_1_r0_d[23:0]), .din(multiplexer_2_out), .data(ram_1_data),
    .str(ula_1_write), .clk(clock_1_out), .ld(ula_1_load));  // open: sel, clr
  Multiplexer #(.width(32)) multiplexer_3 (
    .in0(ula_1_ula_out), .in1(ram_1_data), .out(multiplexer_3_out), .sel(ula_1_load));  // open: en

  // Notes on the sheet:
  //   contents of rom_1 (hex, n*v repeats v):
  //   61500000 40100000 30000000
endmodule

module ULA (
  input  [31:0] in_1,
  input  [31:0] DATA_0,
  input  [31:0] DATA_1,
  input  [3:0] ULA_OP,
  output [31:0] ULA_OUT,
  output bgt,
  output write,
  output load
);

  wire comp_1_jump, comparator_1_gt;
  wire [31:0] adder_1_out, adder_2_out, adder_3_out, multiplier_1_out, subtractor_1_out;

  Adder #(.width(32)) adder_1 (.a(DATA_0), .b(DATA_1), .out(adder_1_out));  // open: cin, cout
  Subtractor #(.width(32)) subtractor_1 (.a(DATA_0), .b(DATA_1), .out(subtractor_1_out));  // open: bin, bout
  Multiplier #(.width(32)) multiplier_1 (.a(DATA_0), .b(DATA_1), .out(multiplier_1_out));  // open: cin, cout
  Adder #(.width(32)) adder_2 (.a(in_1), .b({32{1'b0}}), .out(adder_2_out));  // open: cin, cout
  Comparator #(.width(32), .mode("unsigned")) comparator_1 (
    .a(DATA_1), .b(DATA_0), .gt(comparator_1_gt));  // open: eq, lt
  Adder #(.width(32)) adder_3 (.a(in_1), .b(DATA_0), .out(adder_3_out));  // open: cin, cout
  Multiplexer #(.select(4), .width(32), .enable("false")) multiplexer_1 (
    .in0(adder_1_out), .in1(subtractor_1_out), .in2(multiplier_1_out), .in6(adder_2_out), .in8(adder_3_out),
    .out(ULA_OUT), .sel(ULA_OP));  // open: in3, in4, in5, in7, in9, in10, in11, in12, in13, in14, in15
  comp comp_1 (.E3(ULA_OP[3]), .E2(ULA_OP[2]), .E1(ULA_OP[1]), .E0(ULA_OP[0]), .jump(comp_1_jump));
  STORE store_1 (.ULA_1(ULA_OP[3]), .ULA_2(ULA_OP[2]), .ULA_3(ULA_OP[1]), .ULA_4(ULA_OP[0]), .STORE(write));
  LOAD load_1 (.ULA_1(ULA_OP[3]), .ULA_2(ULA_OP[2]), .ULA_3(ULA_OP[1]), .ULA_4(ULA_OP[0]), .LOAD(load));
  and and_1 (bgt, comparator_1_gt, comp_1_jump);
endmodule

module UC (
  input  E3,
  input  E2,
  input  E1,
  input  E0,
  output ula_op,
  output write_reg,
  output jump
);

  wire not_1_out, not_2_out, not_3_out;

  not not_1 (not_1_out, E3);
  and and_1 (write_reg, not_1_out, not_2_out, not_3_out);
  not not_2 (not_2_out, E2);
  not not_3 (not_3_out, E1);
  jump jump_1 (.E3(E3), .E2(E2), .E1(E1), .E0(E0), .jump(jump));

  assign ula_op = E0;
endmodule

module BANCO_DE_REGISTRADORES (
  input  [31:0] DATA_WRITE,
  input  [3:0] R0,
  input  [3:0] R1,
  input  CLK,
  input  [3:0] RW,
  input  RW_2,
  input  RESET,
  output [31:0] inteiro,
  output [31:0] R0_D,
  output [31:0] R1_D
);

  wire demultiplexer_1_out0, demultiplexer_1_out1, demultiplexer_1_out2, demultiplexer_1_out3,
       demultiplexer_1_out4, demultiplexer_1_out5, demultiplexer_1_out6, demultiplexer_1_out7,
       demultiplexer_1_out8, demultiplexer_1_out9, demultiplexer_1_out10, demultiplexer_1_out11,
       demultiplexer_1_out12, demultiplexer_1_out13, demultiplexer_1_out14, demultiplexer_1_out15;
  wire [31:0] register_1_q, register_2_q, register_3_q, register_4_q, register_5_q, register_6_q,
       register_7_q, register_8_q, register_9_q, register_10_q, register_11_q, register_12_q, register_13_q,
       register_14_q, register_15_q, register_16_q;

  Demultiplexer #(.select(4), .enable("false")) demultiplexer_1 (
    .out0(demultiplexer_1_out0), .out1(demultiplexer_1_out1), .out2(demultiplexer_1_out2),
    .out3(demultiplexer_1_out3), .out4(demultiplexer_1_out4), .out5(demultiplexer_1_out5),
    .out6(demultiplexer_1_out6), .out7(demultiplexer_1_out7), .out8(demultiplexer_1_out8),
    .out9(demultiplexer_1_out9), .out10(demultiplexer_1_out10), .out11(demultiplexer_1_out11),
    .out12(demultiplexer_1_out12), .out13(demultiplexer_1_out13), .out14(demultiplexer_1_out14),
    .out15(demultiplexer_1_out15), .in(RW_2), .sel(RW));
  Register #(.width(32)) register_1 (
    .D(DATA_WRITE), .en(demultiplexer_1_out0), .Q(register_1_q), .clk(CLK), .clr(RESET));
  Register #(.width(32)) register_2 (
    .D(DATA_WRITE), .en(demultiplexer_1_out1), .Q(register_2_q), .clk(CLK), .clr(RESET));
  Register #(.width(32)) register_3 (
    .D(DATA_WRITE), .en(demultiplexer_1_out2), .Q(register_3_q), .clk(CLK), .clr(RESET));
  Register #(.width(32)) register_4 (
    .D(DATA_WRITE), .en(demultiplexer_1_out3), .Q(register_4_q), .clk(CLK), .clr(RESET));
  Register #(.width(32)) register_5 (
    .D(DATA_WRITE), .en(demultiplexer_1_out4), .Q(register_5_q), .clk(CLK), .clr(RESET));
  Register #(.width(32)) register_6 (
    .D(DATA_WRITE), .en(demultiplexer_1_out5), .Q(register_6_q), .clk(CLK), .clr(RESET));
  Register #(.width(32)) register_7 (
    .D(DATA_WRITE), .en(demultiplexer_1_out6), .Q(register_7_q), .clk(CLK), .clr(RESET));
  Register #(.width(32)) register_8 (
    .D(DATA_WRITE), .en(demultiplexer_1_out7), .Q(register_8_q), .clk(CLK), .clr(RESET));
  Register #(.width(32)) register_9 (
    .D(DATA_WRITE), .en(demultiplexer_1_out8), .Q(register_9_q), .clk(CLK), .clr(RESET));
  Register #(.width(32)) register_10 (
    .D(DATA_WRITE), .en(demultiplexer_1_out9), .Q(register_10_q), .clk(CLK), .clr(RESET));
  Register #(.width(32)) register_11 (
    .D(DATA_WRITE), .en(demultiplexer_1_out10), .Q(register_11_q), .clk(CLK), .clr(RESET));
  Register #(.width(32)) register_12 (
    .D(DATA_WRITE), .en(demultiplexer_1_out11), .Q(register_12_q), .clk(CLK), .clr(RESET));
  Register #(.width(32)) register_13 (
    .D(DATA_WRITE), .en(demultiplexer_1_out12), .Q(register_13_q), .clk(CLK), .clr(RESET));
  Register #(.width(32)) register_14 (
    .D(DATA_WRITE), .en(demultiplexer_1_out13), .Q(register_14_q), .clk(CLK), .clr(RESET));
  Register #(.width(32)) register_15 (
    .D(DATA_WRITE), .en(demultiplexer_1_out14), .Q(register_15_q), .clk(CLK), .clr(RESET));
  Register #(.width(32)) register_16 (
    .D(DATA_WRITE), .en(demultiplexer_1_out15), .Q(register_16_q), .clk(CLK), .clr(RESET));
  Multiplexer #(.select(4), .width(32), .disabled(0), .enable("false")) multiplexer_1 (
    .in0(register_1_q), .in1(register_2_q), .in2(register_3_q), .in3(register_4_q), .in4(register_5_q),
    .in5(register_6_q), .in6(register_7_q), .in7(register_8_q), .in8(register_9_q), .in9(register_10_q),
    .in10(register_11_q), .in11(register_12_q), .in12(register_13_q), .in13(register_14_q),
    .in14(register_15_q), .in15(register_16_q), .out(R0_D), .sel(R0));
  Multiplexer #(.select(4), .width(32), .enable("false")) multiplexer_2 (
    .in0(register_1_q), .in1(register_2_q), .in2(register_3_q), .in3(register_4_q), .in4(register_5_q),
    .in5(register_6_q), .in6(register_7_q), .in7(register_8_q), .in8(register_9_q), .in9(register_10_q),
    .in10(register_11_q), .in11(register_12_q), .in12(register_13_q), .in13(register_14_q),
    .in14(register_15_q), .in15(register_16_q), .out(R1_D), .sel(R1));

  assign inteiro = {{28{1'b0}}, R1};
endmodule

module UC_2 (
  input  E3,
  input  E2,
  input  E1,
  input  E0,
  output write_reg,
  output out_6,
  output out_7,
  output out_8
);

  wire and_1_out, and_2_out, and_3_out, not_1_out, not_2_out, not_3_out, not_4_out, not_5_out, not_6_out;

  not not_1 (not_1_out, E3);
  and and_1 (and_1_out, not_1_out, not_2_out);
  not not_2 (not_2_out, E2);
  not not_3 (not_3_out, E3);
  and and_2 (and_2_out, not_3_out, not_4_out, E0);
  not not_4 (not_4_out, E1);
  not not_5 (not_5_out, E3);
  and and_3 (and_3_out, not_5_out, E1, not_6_out);
  not not_6 (not_6_out, E0);
  or or_1 (write_reg, and_1_out, and_2_out, and_3_out);

  assign out_6 = E2;
  assign out_7 = E1;
  assign out_8 = E0;
endmodule

module LOAD (
  input  ULA_1,
  input  ULA_2,
  input  ULA_3,
  input  ULA_4,
  output LOAD
);

  wire not_1_out, not_2_out;

  not not_1 (not_1_out, ULA_1);
  not not_2 (not_2_out, ULA_2);
  and and_1 (LOAD, not_1_out, not_2_out, ULA_3, ULA_4);
endmodule

module STORE (
  input  ULA_1,
  input  ULA_2,
  input  ULA_3,
  input  ULA_4,
  output STORE
);

  wire not_1_out, not_2_out, not_3_out;

  not not_1 (not_1_out, ULA_1);
  not not_2 (not_2_out, ULA_3);
  not not_3 (not_3_out, ULA_4);
  and and_1 (STORE, not_1_out, ULA_2, not_2_out, not_3_out);
endmodule

module UC_4 (
  input  E3,
  input  E2,
  input  E1,
  input  E0,
  output write_reg,
  output [3:0] out_6,
  output jump
);

  wire and_1_out, and_2_out, and_3_out, and_4_out;

  and and_1 (and_1_out, ~E3, ~E2);  // AND_Gate
  and and_2 (and_2_out, ~E2, ~E1, ~E0);  // AND_Gate
  and and_3 (and_3_out, ~E2, ~E1, E0);  // AND_Gate
  and and_4 (and_4_out, ~E3, E1, ~E0);  // AND_Gate
  or or_1 (write_reg, and_1_out, and_2_out, and_3_out, and_4_out);
  jump jump_1 (.E3(E3), .E2(E2), .E1(E1), .E0(E0), .jump(jump));

  assign out_6 = {E3, E2, E1, E0};
endmodule

module jump (
  input  E3,
  input  E2,
  input  E1,
  input  E0,
  output jump
);

  wire and_1_out, and_2_out, not_1_out;

  not not_1 (not_1_out, E1);
  and and_1 (and_1_out, E3, not_1_out, E0);
  and and_2 (and_2_out, E3, E2, E0);
  or or_1 (jump, and_1_out, and_2_out);
endmodule

module comp (
  input  E3,
  input  E2,
  input  E1,
  input  E0,
  output jump
);

  wire and_1_out, and_2_out;

  and and_1 (and_1_out, E2, E1, E0);
  and and_2 (and_2_out, E3, E2, E0);
  or or_1 (jump, and_1_out, and_2_out);
endmodule
